# Fritzing sketch TTGOESP32_DHT11 (saved by Fritzing 0.9.3b)
breadboards: 1

parts:
  DHT11 = Humidity and Temperature Sensor RHT03
  R1 = Resistor [tolerance=±5% resistance=10 package=THT]
  IC1 = IC, DIP package, 36 pins [chip_label=TTGOESP32]

nets:
  N1: DHT11.Vcc, R1.Pin_1, IC1.pin16
  N2: DHT11.Data-signal, R1.Pin_0, IC1.pin3
  N3: DHT11.GND_2, IC1.pin18
